# Fritzing sketch fritzing_diagram (saved by Fritzing 0.9.5d)
breadboards: 1

parts:
  AD8232 = AD8232 HeartRate Monitor [part_number=SEN-12650 chip_label=AD8232 package="DIP (Dual Inline) [THT]"]
  OLED_0_96''_(128X64) = OLED 128x64 I2C Monochrome Display GND-VDD
  Part1 = Arduino Uno (Rev3)
  LED1 = LED - 3mm [color="Red (633nm)" package="3 mm [THT]"]
  LED2 = LED - 3mm [color="Yellow (595nm)" package="3 mm [THT]"]
  LED3 = LED - 3mm [color="Blue (470nm)" package="3 mm [THT]"]
  R1 = Resistor [tolerance=±5% resistance=220 package="1206 [SMD]"]
  R2 = Resistor [tolerance=±5% resistance=220 package="1206 [SMD]"]
  R3 = Resistor [tolerance=±5% resistance=220 package="1206 [SMD]"]
  R4 = Resistor [tolerance=±5% resistance=220 package="1206 [SMD]"]
  Q1 = PNP-Transistor [package="TO92 [THT]"]
  J1 = Piezo Speaker
  R5 = Resistor [tolerance=±5% resistance=220 package="1206 [SMD]"]

nets:
  GND: AD8232.GND, OLED_0_96''_(128X64).GND, Part1.GND, LED1.anode, LED2.anode, LED3.anode, Q1.C
  3.3V: AD8232.3.3v, Part1.3V3
  N1: AD8232.OUTPUT, Part1.A0
  N2: AD8232.LO-, Part1.D11_PWM/MOSI
  N3: AD8232.LO+, Part1.D10_PWM/SS
  VDD: OLED_0_96''_(128X64).VDD, Part1.5V, J1.pin2
  N4: OLED_0_96''_(128X64).SCK, Part1.A5/SCL
  N5: OLED_0_96''_(128X64).SDA, Part1.A4/SDA
  N6: Part1.D8, R2.Pin_0
  N7: Part1.D9_PWM, R3.Pin_0
  N8: Part1.D6_PWM, R4.Pin_0
  N9: Part1.D7, R1.Pin_0
  N10: LED1.cathode, R1.Pin_1
  N11: LED2.cathode, R2.Pin_1
  N12: LED3.cathode, R3.Pin_1
  N13: R4.Pin_1, Q1.B
  N14: Q1.E, R5.Pin_0
  N15: J1.pin1, R5.Pin_1

custom parts:
  AD8232 HeartRate Monitor: A DIP stand-in part for whatever IC you want. With 10 pins on a 600mil dual inline package (DIP) footprint.
  OLED 128x64 I2C Monochrome Display GND-VDD: OLED 128x64 I2C Monochrome Display. Note: there are two variants of this part, this one is the GND VDD SCK SDA variant. The other is VDD GND SCK SDA. Make sure you select the part that matches your module as using the incorrect part will probably destroy your module! In addition the mounting holes are marked on silkscreen but not by default drilled. If you want drilled mounting holes, copy a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
